// Logisim project lab6solution.circ as structural Verilog
module Lab_6_2 (
  input  S2,
  input  S1,
  input  S0,
  input  in1,
  input  in0,
  output n2,
  output n1,
  output n0
);

  wire and_1_out, and_2_out, and_3_out, and_4_out, and_5_out, and_6_out, and_7_out, and_8_out, and_9_out,
       and_10_out, and_11_out, and_12_out, not_1_out, not_2_out, not_3_out, not_4_out, not_5_out, not_6_out,
       not_7_out, not_8_out, not_9_out, not_10_out, not_11_out, not_12_out, not_13_out, not_14_out,
       not_15_out, not_16_out, not_17_out, not_18_out;

  and and_1 (and_1_out, S1, in0);
  and and_2 (and_2_out, S1, S0);
  not not_1 (not_1_out, S1);
  not not_2 (not_2_out, S1);
  not not_3 (not_3_out, S0);
  not not_4 (not_4_out, in0);
  not not_5 (not_5_out, S2);
  not not_6 (not_6_out, S1);
  not not_7 (not_7_out, S0);
  not not_8 (not_8_out, in0);
  not not_9 (not_9_out, S2);
  not not_10 (not_10_out, S0);
  not not_11 (not_11_out, in1);
  not not_12 (not_12_out, in0);
  not not_13 (not_13_out, S1);
  not not_14 (not_14_out, S0);
  not not_15 (not_15_out, in1);
  not not_16 (not_16_out, in0);
  not not_17 (not_17_out, S2);
  not not_18 (not_18_out, in1);
  or or_1 (n2, in1, and_1_out, and_2_out, S2);
  and and_3 (and_3_out, not_1_out, in0);
  and and_4 (and_4_out, not_2_out, S0);
  and and_5 (and_5_out, S1, not_3_out, not_4_out);
  and and_6 (and_6_out, S1, in1);
  and and_7 (and_7_out, S2, in1);
  and and_8 (and_8_out, S2, S1);
  and and_9 (and_9_out, not_5_out, not_6_out, not_7_out, not_8_out);
  and and_10 (and_10_out, not_9_out, not_10_out, not_11_out, not_12_out);
  and and_11 (and_11_out, not_13_out, not_14_out, not_15_out, not_16_out);
  and and_12 (and_12_out, not_17_out, S0, not_18_out, in0);
  or or_2 (n1, and_3_out, and_4_out, and_5_out, and_6_out, and_7_out, and_8_out);
  or or_3 (n0, and_9_out, and_10_out, and_11_out, and_12_out);
endmodule

module Lab_6_1 (
  input  S1,
  input  S0,
  input  in,
  output n1,
  output n0
);

  wire and_1_out, and_2_out, not_1_out, not_2_out;

  not not_1 (not_1_out, S1);
  not not_2 (not_2_out, in);
  not not_3 (n0, S0);
  and and_1 (and_1_out, not_1_out, in);
  and and_2 (and_2_out, S1, not_2_out);
  or or_1 (n1, and_1_out, and_2_out);
endmodule
